# Fritzing sketch SmartMixer (saved by Fritzing 0.9.3b)

parts:
  Part1 = Arduino Mega 2560 (Rev3)
  A1 = DHT22 module
  microSD1 = MicroSD Card Module
  C1 = Electrolytic Capacitor [package="2cm H-Type"]
  Part2 = HX711 Weighing Sensor Module
  S1 = Round Pushbutton
  S2 = Round Pushbutton
  S3 = Round Pushbutton
  RY1 = SSR-40VA
  M1 = 1 chan 5v relay module
  Part3 = LCD1602-I2C
  S4 = PH meter [package=THT]
  HLK-PM1 = HLK-PM12 [part_number=HLK-PM12]
  HLK-PM2 = HLK-PM01

nets:
  N1: Part1.A0, S4.pin1
  N2: Part1.D21/SCL, Part3.SCL
  N3: Part1.D20/SDA, Part3.SDA
  GND: Part1.GND, A1.-, microSD1.GND, C1.-, Part2.GND, S1.leg1, S2.leg1, S3.leg1, RY1.Pin_4, M1.pin_2, Part3.GND, S4.pin3, HLK-PM2.-Vo
  VCC: Part1.VIN, A1.+, microSD1.VCC, C1.+, Part2.VCC, M1.pin_1, Part3.VCC, S4.pin2, HLK-PM2.+Vo
  N4: Part1.D2_PWM, A1.Out
  N5: Part1.D3_PWM, Part2.CK/TX
  N6: Part1.D4_PWM, Part2.DO/RX
  N7: Part1.D5_PWM, S3.leg0
  N8: Part1.D6_PWM, S2.leg0
  N9: Part1.D22, M1.pin_3
  N10: Part1.D23, RY1.Pin_3
  N11: Part1.D24, S1.leg0
  N12: Part1.D50, microSD1.MISO
  N13: Part1.D51, microSD1.MOSI
  N14: Part1.D52, microSD1.SCK
  N15: Part1.D53, microSD1.CS
  N16: M1.pin_5, HLK-PM1.+Vo

custom parts:
  DHT22 module: DHT22 module. Pins VCC Data GND.
  SSR-40VA: SSR-40VA solid state relay.
  1 chan 5v relay module: 1 Channel 5V Relay Module Board Shield with Optocoupler Support High and Low Level Trigger for Arduino.
  LCD1602-I2C: A standard character display, usually with 2x16 characters. Comes in many colors with LCM1602 IIC attached.
